// Logisim project processor-suprise.circ as structural Verilog: 6 circuits, main circuit main
module main (
);

  ALU alu_1 ();  // open: F, B, A, Y, Zero
  Datapath datapath_1 ();  // open: out_8, out_5, out_11, v0, v0_2, v0_3, v0_4, v0_5, v0_6, v0_7, v0_8, v0_9, v0_10
endmodule

module ALU (
  input  [31:0] B,
  input  [31:0] A,
  input  [2:0] F,
  output [31:0] Y,
  output Zero
);

  wire bitselector_1_out, or_2_out;
  wire [31:0] adder_1_out, and_1_out, bit_extender_1_out, multiplexer_1_out, multiplier_1_out, not_1_out,
       or_1_out;

  Multiplexer #(.width(32)) multiplexer_1 (.in0(B), .in1(not_1_out), .out(multiplexer_1_out), .sel(F[2]));  // open: en
  assign not_1_out = ~B;  // NOT_Gate not_1, 32 bits wide
  Adder #(.width(32)) adder_1 (.a(multiplexer_1_out), .b(A), .out(adder_1_out), .cin(F[2]));  // open: cout
  Multiplier #(.width(32)) multiplier_1 (.a(B), .b(A), .out(multiplier_1_out));  // open: cin, cout
  assign and_1_out = multiplexer_1_out & A;  // AND_Gate and_1, 32 bits wide
  assign or_1_out = multiplexer_1_out | A;  // OR_Gate or_1, 32 bits wide
  BitSelector #(.width(32)) bitselector_1 (.in(adder_1_out), .out(bitselector_1_out), .sel({5{1'b0}}));
  assign bit_extender_1_out = {{31{1'b0}}, bitselector_1_out};  // Bit_Extender bit_extender_1
  Multiplexer #(.select(3), .width(32)) multiplexer_2 (
    .in0(and_1_out), .in1(or_1_out), .in2(adder_1_out), .in3(multiplier_1_out), .in6(adder_1_out),
    .in7(bit_extender_1_out), .out(Y), .sel(F));  // open: in4, in5, en
  not not_2 (Zero, or_2_out);
  or or_2 (or_2_out, Y[0], Y[1], Y[2], Y[3], Y[4], Y[5], Y[6], Y[7], Y[8], Y[9], Y[10], Y[11], Y[12], Y[13], Y[14], Y[15], Y[16], Y[17], Y[18], Y[19], Y[20], Y[21], Y[22], Y[23], Y[24], Y[25], Y[26], Y[27], Y[28], Y[29], Y[30], Y[31]);

  // Notes on the sheet:
  //   And function
  //   OR function
  //   Set less than function
  //   Output 
endmodule

module Datapath (
  output [2:0] v0,
  output [31:0] v0_2,
  output [31:0] v0_3,
  output [2:0] v0_4,
  output [3:0] out_5,
  output [31:0] v0_5,
  output [7:0] v0_6,
  output [3:0] out_8,
  output [31:0] v0_7,
  output [7:0] v0_8,
  output [10:0] out_11,
  output [31:0] v0_9,
  output [7:0] v0_10
);

  wire alu_1_zero, and_1_out, clock_1_out, controlunit_1_alusrc, controlunit_1_branch, controlunit_1_regdst,
       controlunit_1_regwrite;
  wire [2:0] bitselector_3_out, bitselector_7_out, bitselector_8_out, multiplexer_2_out;
  wire [7:0] bitselector_6_out, bitselector_9_out, multiplexer_1_out, register_1_q, shifter_1_out;
  wire [31:0] bit_extender_1_out, registerfile_1_rd2;

  Clock clock_1 (.out(clock_1_out));
  Multiplexer #(.width(8)) multiplexer_1 (
    .in0(v0_6), .in1(v0_8), .out(multiplexer_1_out), .sel(and_1_out));  // open: en
  Register register_1 (.D(multiplexer_1_out), .Q(register_1_q), .clk(clock_1_out));  // open: en, clr
  Shifter #(.shift("lr")) shifter_1 (.in(register_1_q), .\dist (3'b010), .out(shifter_1_out));
  Adder adder_1 (.a(register_1_q), .b(8'h4), .out(v0_6));  // open: cin, cout
  ROM #(.dataWidth(32)) rom_1 (.addr(shifter_1_out), .data(v0_2));  // open: sel
  BitSelector #(.width(32), .group(3)) bitselector_1 (.in(v0_2), .out(v0_4), .sel(4'b0111));
  BitSelector #(.width(32), .group(4)) bitselector_2 (.in(v0_2), .out(out_5), .sel(3'b100));
  ControlUnit controlunit_1 (
    .Instruction(v0_2), .RegDst(controlunit_1_regdst), .RegWrite(controlunit_1_regwrite), .ALUControl(v0),
    .Branch(controlunit_1_branch), .ALUSrc(controlunit_1_alusrc));
  BitSelector #(.width(4), .group(3)) bitselector_3 (.in(out_5), .out(bitselector_3_out), .sel(1'b0));
  BitSelector #(.width(32), .group(4)) bitselector_4 (.in(v0_2), .out(out_8), .sel(3'b100));
  BitSelector #(.width(32), .group(11)) bitselector_5 (.in(v0_2), .out(out_11), .sel(2'b01));
  assign bit_extender_1_out = {{24{bitselector_6_out[7]}}, bitselector_6_out};  // Bit_Extender bit_extender_1
  BitSelector #(.width(32), .group(8)) bitselector_6 (.in(v0_2), .out(bitselector_6_out), .sel(2'b00));
  RegisterFile registerfile_1 (
    .CLK(clock_1_out), .A1(v0_4), .WD3(v0_5), .A2(bitselector_3_out), .WE3(controlunit_1_regwrite),
    .RD1(v0_3), .RD2(registerfile_1_rd2), .A3(multiplexer_2_out));  // open: V0
  BitSelector #(.width(4), .group(3)) bitselector_7 (.in(out_8), .out(bitselector_7_out), .sel(1'b0));
  BitSelector #(.width(11), .group(3)) bitselector_8 (.in(out_11), .out(bitselector_8_out), .sel(2'b00));
  Multiplexer #(.width(3)) multiplexer_2 (
    .in0(bitselector_7_out), .in1(bitselector_8_out), .out(multiplexer_2_out), .sel(controlunit_1_regdst));  // open: en
  Shifter #(.width(32)) shifter_2 (.in(bit_extender_1_out), .\dist (5'b00010), .out(v0_9));
  Multiplexer #(.width(32)) multiplexer_3 (
    .in0(registerfile_1_rd2), .in1(bit_extender_1_out), .out(v0_7), .sel(controlunit_1_alusrc));  // open: en
  BitSelector #(.width(32), .group(8)) bitselector_9 (.in(v0_9), .out(bitselector_9_out), .sel(2'b00));
  and and_1 (and_1_out, controlunit_1_branch, alu_1_zero);
  ALU alu_1 (.F(v0), .B(v0_7), .A(v0_3), .Y(v0_5), .Zero(alu_1_zero));
  Adder adder_2 (.a(bitselector_9_out), .b(v0_6), .out(v0_8));  // open: cin, cout

  assign v0_10 = v0_8;

  // Notes on the sheet:
  //   contents of rom_1 (hex, n*v repeats v):
  //   20040008 10800007 20820000 2084ffff 10800004 20 70441002 1000fffb 20 1042ffff
endmodule

module Tests (
  output [31:0] Y,
  output [7:0] out_2,
  output [7:0] out_3,
  output [3:0] out_4
);

  BitSelector #(.width(32), .group(8)) bitselector_1 (.in(32'h12356789), .out(out_2), .sel(2'b00));
  BitSelector #(.width(32), .group(8)) bitselector_2 (.in(32'h12356789), .out(out_3), .sel(2'b00));
  BitSelector #(.group(4)) bitselector_3 (.in(out_3), .out(out_4), .sel(1'b0));

  assign Y = 32'hf4010207;

  // Notes on the sheet:
  //   binary values in Logisim. Convince yourself how the bits are displayed.
  //   Example 2: The bit selector is configured to have 32  
  //   bit group #1 (starting at index 0) is selected for the output.
  //   That is, the 8 bits 0x67 at bit indices 15..8  are sent to the output.
  //   Example 3: Now, assume that you want to extract 3 bits at   
  //   Example 1: A simple example that illustrates how 32-bit values are displayed as 
  //   input bits and 8 output bits. The parameter constant is 1, which means that   
  //   bit indices 10..8. This can be accoplished by putting two bit selecotrs in series.
endmodule

module RegisterFile (
  input  CLK,
  input  [2:0] A1,
  input  [31:0] WD3,
  input  [2:0] A2,
  input  WE3,
  input  [2:0] A3,
  output [31:0] RD1,
  output [31:0] RD2,
  output [31:0] V0
);

  wire and_1_out, and_2_out, and_3_out, and_4_out, and_5_out, and_6_out, and_7_out, decoder_1_out0,
       decoder_1_out1, decoder_1_out2, decoder_1_out3, decoder_1_out4, decoder_1_out5, decoder_1_out6,
       decoder_1_out7;
  wire [31:0] bit_extender_1_out, register_1_q, register_3_q, register_4_q, register_5_q, register_6_q,
       register_7_q;

  Decoder #(.select(3)) decoder_1 (
    .out0(decoder_1_out0), .out1(decoder_1_out1), .out2(decoder_1_out2), .out3(decoder_1_out3),
    .out4(decoder_1_out4), .out5(decoder_1_out5), .out6(decoder_1_out6), .out7(decoder_1_out7), .sel(A3));  // open: en
  and and_1 (and_1_out, WE3, decoder_1_out1);
  and and_2 (and_2_out, WE3, decoder_1_out2);
  and and_3 (and_3_out, WE3, decoder_1_out3);
  and and_4 (and_4_out, WE3, decoder_1_out4);
  and and_5 (and_5_out, WE3, decoder_1_out5);
  and and_6 (and_6_out, WE3, decoder_1_out6);
  and and_7 (and_7_out, WE3, decoder_1_out7);
  assign bit_extender_1_out = {{31{1'b0}}, 1'b0};  // Bit_Extender bit_extender_1
  Register #(.width(32)) register_1 (.D(WD3), .en(and_1_out), .Q(register_1_q), .clk(CLK));  // open: clr
  Register #(.width(32)) register_2 (.D(WD3), .en(and_2_out), .Q(V0), .clk(CLK));  // open: clr
  Register #(.width(32)) register_3 (.D(WD3), .en(and_3_out), .Q(register_3_q), .clk(CLK));  // open: clr
  Register #(.width(32)) register_4 (.D(WD3), .en(and_4_out), .Q(register_4_q), .clk(CLK));  // open: clr
  Register #(.width(32)) register_5 (.D(WD3), .en(and_5_out), .Q(register_5_q), .clk(CLK));  // open: clr
  Register #(.width(32)) register_6 (.D(WD3), .en(and_6_out), .Q(register_6_q), .clk(CLK));  // open: clr
  Register #(.width(32)) register_7 (.D(WD3), .en(and_7_out), .Q(register_7_q), .clk(CLK));  // open: clr
  Multiplexer #(.select(3), .width(32)) multiplexer_1 (
    .in0(bit_extender_1_out), .in1(register_1_q), .in2(V0), .in3(register_3_q), .in4(register_4_q),
    .in5(register_5_q), .in6(register_6_q), .in7(register_7_q), .out(RD1), .sel(A1));  // open: en
  Multiplexer #(.select(3), .width(32)) multiplexer_2 (
    .in0(bit_extender_1_out), .in1(register_1_q), .in2(V0), .in3(register_3_q), .in4(register_4_q),
    .in5(register_5_q), .in6(register_6_q), .in7(register_7_q), .out(RD2), .sel(A2));  // open: en
endmodule

module ControlUnit (
  input  [31:0] Instruction,
  output RegDst,
  output RegWrite,
  output ALUSrc,
  output Branch,
  output [2:0] ALUControl
);

  wire comparator_3_eq;
  wire [5:0] bitselector_1_out;
  wire [31:0] shifter_1_out;

  Shifter #(.width(32), .shift("lr")) shifter_1 (.in(Instruction), .\dist (5'b11010), .out(shifter_1_out));
  BitSelector #(.width(32), .group(6)) bitselector_1 (.in(shifter_1_out), .out(bitselector_1_out), .sel(3'b000));
  Comparator #(.width(6), .mode("unsigned")) comparator_1 (
    .a(bitselector_1_out), .b(6'b011100), .eq(ALUControl[0]));  // open: gt, lt
  Comparator #(.width(6), .mode("unsigned")) comparator_2 (
    .a(bitselector_1_out), .b(6'b001000), .eq(ALUSrc));  // open: gt, lt
  Comparator #(.width(6), .mode("unsigned")) comparator_3 (
    .a(bitselector_1_out), .b({6{1'b0}}), .eq(comparator_3_eq));  // open: gt, lt
  Comparator #(.width(6), .mode("unsigned")) comparator_4 (
    .a(bitselector_1_out), .b(6'b000100), .eq(ALUControl[2]));  // open: gt, lt
  or or_1 (RegDst, ALUControl[0], comparator_3_eq);
  or or_2 (RegWrite, ALUSrc, ALUControl[0], comparator_3_eq);

  assign ALUControl[1] = 1'b1;
  assign Branch = ALUControl[2];
endmodule
