// Logisim project processor.circ as structural Verilog: 6 circuits, main circuit main
module main (
);

  ALU alu_1 ();  // open: F, B, A, Y, Zero, in_3
  Datapath datapath_1 ();  // open: out_3, out_2, out_4, v0
endmodule

module ALU (
  input  [31:0] B,
  input  [31:0] A,
  input  [4:0] in_3,
  input  [2:0] F,
  output [31:0] Y,
  output Zero
);

  wire bitselector_1_out, or_2_out;
  wire [31:0] adder_1_out, and_1_out, bit_extender_1_out, multiplexer_1_out, not_1_out, or_1_out;

  Multiplexer #(.width(32)) multiplexer_1 (.in0(B), .in1(not_1_out), .out(multiplexer_1_out), .sel(F[2]));  // open: en
  assign not_1_out = ~B;  // NOT_Gate not_1, 32 bits wide
  assign and_1_out = multiplexer_1_out & A;  // AND_Gate and_1, 32 bits wide
  assign or_1_out = multiplexer_1_out | A;  // OR_Gate or_1, 32 bits wide
  Adder #(.width(32)) adder_1 (.a(multiplexer_1_out), .b(A), .out(adder_1_out), .cin(F[2]));  // open: cout
  BitSelector #(.width(32)) bitselector_1 (.in(adder_1_out), .out(bitselector_1_out), .sel(in_3));
  assign bit_extender_1_out = {{31{1'b0}}, bitselector_1_out};  // Bit_Extender bit_extender_1
  Multiplexer #(.select(3), .width(32)) multiplexer_2 (
    .in0(and_1_out), .in1(or_1_out), .in2(adder_1_out), .in4(adder_1_out), .in5(bit_extender_1_out), .out(Y),
    .sel(F));  // open: in3, in6, in7, en
  or or_2 (or_2_out, Y[0], Y[1], Y[2], Y[3], Y[4], Y[5], Y[6], Y[7], Y[8], Y[9], Y[10], Y[11], Y[12], Y[13], Y[14], Y[15], Y[16], Y[17], Y[18], Y[19], Y[20], Y[21], Y[22], Y[23], Y[24], Y[25], Y[26], Y[27], Y[28], Y[29], Y[30], Y[31]);
  not not_2 (Zero, or_2_out);

  // Notes on the sheet:
  //   And function
  //   OR function
  //   Set less than function
  //   Output 
endmodule

module Datapath (
  output [31:0] v0,
  output [3:0] out_2,
  output [3:0] out_3,
  output [10:0] out_4
);

  wire alu_1_zero, and_1_out, clock_1_out, controlunit_1_alusrc, controlunit_1_branch, controlunit_1_regdst,
       controlunit_1_regwrite;
  wire [2:0] bitselector_3_out, bitselector_5_out, bitselector_9_out, bitselector_10_out,
       controlunit_1_alucontrol, multiplexer_2_out;
  wire [7:0] bitselector_1_out, bitselector_2_out, bitselector_8_out, multiplexer_1_out, register_1_q,
       shifter_1_out;
  wire [31:0] adder_2_out, alu_1_y, bit_extender_1_out, multiplexer_3_out, registerfile_1_rd1,
       registerfile_1_rd2, rom_1_data, shifter_2_out, undriven;

  BitSelector #(.width(32), .group(8)) bitselector_1 (.in(undriven), .out(bitselector_1_out), .sel(2'b00));
  BitSelector #(.width(32), .group(8)) bitselector_2 (.in(adder_2_out), .out(bitselector_2_out), .sel(2'b00));
  Clock clock_1 (.out(clock_1_out));
  Register register_1 (.D(multiplexer_1_out), .Q(register_1_q), .clk(clock_1_out));  // open: en, clr
  Multiplexer #(.width(8)) multiplexer_1 (
    .in0(bitselector_1_out), .in1(bitselector_2_out), .out(multiplexer_1_out), .sel(and_1_out));  // open: en
  Shifter #(.shift("lr")) shifter_1 (.in(register_1_q), .\dist (3'b010), .out(shifter_1_out));
  Adder adder_1 (.a(register_1_q), .b(8'h4), .out(bitselector_1_out));  // open: cin, cout
  ROM #(.dataWidth(32)) rom_1 (.addr(shifter_1_out), .data(rom_1_data));  // open: sel
  BitSelector #(.width(32), .group(3)) bitselector_3 (.in(rom_1_data), .out(bitselector_3_out), .sel(4'b0111));
  BitSelector #(.width(32), .group(4)) bitselector_4 (.in(rom_1_data), .out(out_2), .sel(3'b100));
  ControlUnit controlunit_1 (
    .Instruction(rom_1_data), .RegDst(controlunit_1_regdst), .RegWrite(controlunit_1_regwrite),
    .ALUControl(controlunit_1_alucontrol), .Branch(controlunit_1_branch), .ALUSrc(controlunit_1_alusrc));
  BitSelector #(.width(4), .group(3)) bitselector_5 (.in(out_2), .out(bitselector_5_out), .sel(1'b0));
  BitSelector #(.width(32), .group(4)) bitselector_6 (.in(rom_1_data), .out(out_3), .sel(3'b100));
  BitSelector #(.width(32), .group(11)) bitselector_7 (.in(rom_1_data), .out(out_4), .sel(2'b01));
  assign bit_extender_1_out = {{24{bitselector_8_out[7]}}, bitselector_8_out};  // Bit_Extender bit_extender_1
  BitSelector #(.width(32), .group(8)) bitselector_8 (.in(rom_1_data), .out(bitselector_8_out), .sel(2'b00));
  RegisterFile registerfile_1 (
    .CLK(clock_1_out), .A1(bitselector_3_out), .WD3(alu_1_y), .A2(bitselector_5_out),
    .WE3(controlunit_1_regwrite), .RD1(registerfile_1_rd1), .RD2(registerfile_1_rd2), .A3(multiplexer_2_out));  // open: V0, in_5
  BitSelector #(.width(4), .group(3)) bitselector_9 (.in(out_3), .out(bitselector_9_out), .sel(1'b0));
  BitSelector #(.width(11), .group(3)) bitselector_10 (.in(out_4), .out(bitselector_10_out), .sel(2'b00));
  Multiplexer #(.width(3)) multiplexer_2 (
    .in0(bitselector_9_out), .in1(bitselector_10_out), .out(multiplexer_2_out), .sel(controlunit_1_regdst));  // open: en
  Multiplexer #(.width(32)) multiplexer_3 (
    .in0(registerfile_1_rd2), .in1(bit_extender_1_out), .out(multiplexer_3_out), .sel(controlunit_1_alusrc));  // open: en
  and and_1 (and_1_out, controlunit_1_branch, alu_1_zero);
  Shifter #(.width(32)) shifter_2 (.in(bit_extender_1_out), .\dist (5'b00010), .out(shifter_2_out));
  ALU alu_1 (
    .F(controlunit_1_alucontrol), .B(multiplexer_3_out), .A(registerfile_1_rd1), .Y(alu_1_y),
    .Zero(alu_1_zero));  // open: in_3
  Adder #(.width(32)) adder_2 (.a(shifter_2_out), .b(undriven), .out(adder_2_out));  // open: cin, cout

  // Notes on the sheet:
  //   contents of rom_1 (hex, n*v repeats v):
  //   20040004 20820002 441020 10440002 2042fffd 1000fffd 20
endmodule

module Tests (
  output [31:0] Y,
  output [7:0] out_2,
  output [7:0] out_3,
  output [3:0] out_4
);

  BitSelector #(.width(32), .group(8)) bitselector_1 (.in(32'h12356789), .out(out_2), .sel(2'b00));
  BitSelector #(.width(32), .group(8)) bitselector_2 (.in(32'h12356789), .out(out_3), .sel(2'b00));
  BitSelector #(.group(4)) bitselector_3 (.in(out_3), .out(out_4), .sel(1'b0));

  assign Y = 32'hf4010207;

  // Notes on the sheet:
  //   binary values in Logisim. Convince yourself how the bits are displayed.
  //   Example 2: The bit selector is configured to have 32  
  //   bit group #1 (starting at index 0) is selected for the output.
  //   That is, the 8 bits 0x67 at bit indices 15..8  are sent to the output.
  //   Example 3: Now, assume that you want to extract 3 bits at   
  //   Example 1: A simple example that illustrates how 32-bit values are displayed as 
  //   input bits and 8 output bits. The parameter constant is 1, which means that   
  //   bit indices 10..8. This can be accoplished by putting two bit selecotrs in series.
endmodule

module RegisterFile (
  input  CLK,
  input  [2:0] A1,
  input  [31:0] WD3,
  input  [2:0] A2,
  input  in_5,
  input  WE3,
  input  [2:0] A3,
  output [31:0] RD1,
  output [31:0] RD2,
  output [31:0] V0
);

  wire and_1_out, and_2_out, and_3_out, and_4_out, and_5_out, and_6_out, and_7_out, decoder_1_out0,
       decoder_1_out1, decoder_1_out2, decoder_1_out3, decoder_1_out4, decoder_1_out5, decoder_1_out6,
       decoder_1_out7;
  wire [31:0] bit_extender_1_out, register_1_q, register_3_q, register_4_q, register_5_q, register_6_q,
       register_7_q;

  Decoder #(.select(3)) decoder_1 (
    .out0(decoder_1_out0), .out1(decoder_1_out1), .out2(decoder_1_out2), .out3(decoder_1_out3),
    .out4(decoder_1_out4), .out5(decoder_1_out5), .out6(decoder_1_out6), .out7(decoder_1_out7), .sel(A3));  // open: en
  and and_1 (and_1_out, WE3, decoder_1_out1);
  and and_2 (and_2_out, WE3, decoder_1_out2);
  and and_3 (and_3_out, WE3, decoder_1_out3);
  and and_4 (and_4_out, WE3, decoder_1_out4);
  and and_5 (and_5_out, WE3, decoder_1_out5);
  and and_6 (and_6_out, WE3, decoder_1_out6);
  and and_7 (and_7_out, WE3, decoder_1_out7);
  assign bit_extender_1_out = {{31{1'b0}}, in_5};  // Bit_Extender bit_extender_1
  Register #(.width(32)) register_1 (.D(WD3), .en(and_1_out), .Q(register_1_q), .clk(CLK));  // open: clr
  Register #(.width(32)) register_2 (.D(WD3), .en(and_2_out), .Q(V0), .clk(CLK));  // open: clr
  Register #(.width(32)) register_3 (.D(WD3), .en(and_3_out), .Q(register_3_q), .clk(CLK));  // open: clr
  Register #(.width(32)) register_4 (.D(WD3), .en(and_4_out), .Q(register_4_q), .clk(CLK));  // open: clr
  Register #(.width(32)) register_5 (.D(WD3), .en(and_5_out), .Q(register_5_q), .clk(CLK));  // open: clr
  Register #(.width(32)) register_6 (.D(WD3), .en(and_6_out), .Q(register_6_q), .clk(CLK));  // open: clr
  Register #(.width(32)) register_7 (.D(WD3), .en(and_7_out), .Q(register_7_q), .clk(CLK));  // open: clr
  Multiplexer #(.select(3), .width(32)) multiplexer_1 (
    .in0(bit_extender_1_out), .in1(register_1_q), .in2(V0), .in3(register_3_q), .in4(register_4_q),
    .in5(register_5_q), .in6(register_6_q), .in7(register_7_q), .out(RD1), .sel(A1));  // open: en
  Multiplexer #(.select(3), .width(32)) multiplexer_2 (
    .in0(bit_extender_1_out), .in1(register_1_q), .in2(V0), .in3(register_3_q), .in4(register_4_q),
    .in5(register_5_q), .in6(register_6_q), .in7(register_7_q), .out(RD2), .sel(A2));  // open: en
endmodule

module ControlUnit (
  input  [31:0] Instruction,
  output RegDst,
  output RegWrite,
  output ALUSrc,
  output Branch,
  output [2:0] ALUControl
);

  wire [5:0] bitselector_1_out;
  wire [31:0] shifter_1_out;

  Shifter #(.width(32), .shift("lr")) shifter_1 (.in(Instruction), .\dist (5'b11010), .out(shifter_1_out));
  BitSelector #(.width(32), .group(6)) bitselector_1 (.in(shifter_1_out), .out(bitselector_1_out), .sel(3'b000));
  Comparator #(.width(6), .mode("unsigned")) comparator_1 (
    .a(bitselector_1_out), .b(6'b001000), .eq(ALUSrc));  // open: gt, lt
  Comparator #(.width(6), .mode("unsigned")) comparator_2 (
    .a(bitselector_1_out), .b({6{1'b0}}), .eq(RegDst));  // open: gt, lt
  Comparator #(.width(6), .mode("unsigned")) comparator_3 (
    .a(bitselector_1_out), .b(6'b000100), .eq(ALUControl[2]));  // open: gt, lt
  or or_1 (RegWrite, ALUSrc, RegDst);

  assign ALUControl[1:0] = 2'b10;
  assign Branch = ALUControl[2];
endmodule
